# Fritzing sketch example-setup (saved by Fritzing 0.9.3b)
perfboards: 3
stripboards: 3

parts:
  R1 = Resistor [tolerance=±5% resistance=10k package="0603 [SMD]"]
  R2 = Resistor [tolerance=±5% resistance=15k package=THT]
  S1 = Pushbutton [package="[THT]"]
  S2 = Pushbutton [package="[THT]"]

nets:
  N1: R1.Pin_0, R2.Pin_0
  N2: R2.Pin_1, S1.Pin_3, S1.Pin_4, S2.Pin_3, S2.Pin_4
  N3: S1.Pin_1, S1.Pin_2
  N4: S2.Pin_1, S2.Pin_2
